// Logisim project cpu.circ as structural Verilog: 5 circuits, main circuit main
module main (
  input  WE,
  input  [7:0] Testing_Data,
  input  OE_Testing_Data,
  input  OE,
  input  Internal_OE,
  input  WE_2,
  input  WE_3,
  input  OE_2,
  input  OE_3,
  input  WE_4,
  input  WE_5,
  input  OE_4,
  input  OE_5,
  input  WE_6,
  output [3:0] MAR_Conten,
  output [7:0] IR_Content,
  output [7:0] MBR_Content,
  output [7:0] Reg_A_Content,
  output [7:0] out_19,
  output [7:0] ALU_Result,
  output [7:0] Reg_B_Content
);

  wire Clock_out;
  wire [3:0] bitselector_1_out, mar_1_dout;
  wire [7:0] ALU_dout, register_1_dout;

  Clock Clock (.out(Clock_out));
  Register register_1 (
    .Clock(Clock_out), .WE(WE_2), .Din(ALU_dout), .OE(OE_3), .Dout(register_1_dout), .Stored_Data(IR_Content));
  Register Register_A (.Clock(Clock_out), .WE(WE_4), .Din(ALU_dout), .Stored_Data(Reg_A_Content));  // open: OE, Dout
  ALU ALU (
    .Reg_A(Reg_A_Content), .Reg_B(Reg_B_Content), .OE(OE_5), .Dout(ALU_dout), .ALU_Result(ALU_Result));  // open: Carry_Out
  Register Register_B (.Clock(Clock_out), .WE(WE_6), .Din(ALU_dout), .Stored_Data(Reg_B_Content));  // open: OE, Dout
  BitSelector #(.group(4)) bitselector_1 (.in(register_1_dout), .out(bitselector_1_out), .sel(1'b0));
  LED D7 (.in(ALU_dout[7]));
  assign ALU_dout = OE_Testing_Data ? Testing_Data : 8'bz;  // Controlled_Buffer controlled_buffer_1
  LED D4 (.in(ALU_dout[4]));
  LED D5 (.in(ALU_dout[5]));
  LED D3 (.in(ALU_dout[3]));
  LED D6 (.in(ALU_dout[6]));
  LED D2 (.in(ALU_dout[2]));
  LED D0 (.in(ALU_dout[0]));
  LED D1 (.in(ALU_dout[1]));
  MAR mar_1 (.Clock(Clock_out), .WE(WE), .Din(bitselector_1_out), .OE(OE), .Dout(mar_1_dout), .Stored_Data(MAR_Conten));
  assign ALU_dout = Internal_OE ? MBR_Content : 8'bz;  // Controlled_Buffer controlled_buffer_2
  Register MBR (.Clock(Clock_out), .WE(WE_3), .Din(ALU_dout), .OE(OE_2), .Dout(ALU_dout), .Stored_Data(MBR_Content));
  Register register_2 (.Clock(Clock_out), .WE(WE_5), .Din(ALU_dout), .OE(OE_4), .Dout(ALU_dout), .Stored_Data(out_19));
  LED D7_2 (.in(ALU_dout[7]));
  LED D6_2 (.in(ALU_dout[6]));
  LED D5_2 (.in(ALU_dout[5]));
  LED D4_2 (.in(ALU_dout[4]));
  LED D1_2 (.in(ALU_dout[1]));
  LED D2_2 (.in(ALU_dout[2]));
  LED D3_2 (.in(ALU_dout[3]));
  LED D0_2 (.in(ALU_dout[0]));

  // Notes on the sheet:
  //   Instuction Register
  //   Internal Address Bus (4 Bits)
  //   Internal Data Bus
  //   MAR
  //   Output Register
  //   Eksternal Address Bus
  //   Eksternal Data Bus
endmodule

module Memory_Cell (
  input  Clock,
  input  WE,
  input  Din,
  input  OE,
  input  Reset,
  output Dout,
  output Stored_Data
);

  wire and_1_out, and_2_out, not_1_out, or_1_out;

  not not_1 (not_1_out, WE);
  and and_1 (and_1_out, Stored_Data, not_1_out);
  and and_2 (and_2_out, WE, Din);
  or or_1 (or_1_out, and_1_out, and_2_out);
  D_Flip_Flop d_ff_1 (.clk(Clock), .D(or_1_out), .Q(Stored_Data), .reset(Reset));  // open: Qn, preset, en
  assign Dout = OE ? Stored_Data : 1'bz;  // Controlled_Buffer controlled_buffer_1

  // Notes on the sheet:
  //   Memory Cell
endmodule

module Register (
  input  Clock,
  input  WE,
  input  [7:0] Din,
  input  OE,
  output [7:0] Dout,
  output [7:0] Stored_Data
);

  Memory_Cell o (
    .Clock(Clock), .WE(WE), .Din(Din[0]), .OE(OE), .Dout(Dout[0]), .Stored_Data(Stored_Data[0]));  // open: Reset
  Memory_Cell _1 (
    .Clock(Clock), .WE(WE), .Din(Din[1]), .OE(OE), .Dout(Dout[1]), .Stored_Data(Stored_Data[1]));  // open: Reset
  Memory_Cell _2 (
    .Clock(Clock), .WE(WE), .Din(Din[2]), .OE(OE), .Dout(Dout[2]), .Stored_Data(Stored_Data[2]));  // open: Reset
  Memory_Cell _3 (
    .Clock(Clock), .WE(WE), .Din(Din[3]), .OE(OE), .Dout(Dout[3]), .Stored_Data(Stored_Data[3]));  // open: Reset
  Memory_Cell _4 (
    .Clock(Clock), .WE(WE), .Din(Din[4]), .OE(OE), .Dout(Dout[4]), .Stored_Data(Stored_Data[4]));  // open: Reset
  Memory_Cell _5 (
    .Clock(Clock), .WE(WE), .Din(Din[5]), .OE(OE), .Dout(Dout[5]), .Stored_Data(Stored_Data[5]));  // open: Reset
  Memory_Cell _6 (
    .Clock(Clock), .WE(WE), .Din(Din[6]), .OE(OE), .Dout(Dout[6]), .Stored_Data(Stored_Data[6]));  // open: Reset
  Memory_Cell _7 (
    .Clock(Clock), .WE(WE), .Din(Din[7]), .OE(OE), .Dout(Dout[7]), .Stored_Data(Stored_Data[7]));  // open: Reset

  // Notes on the sheet:
  //   Register (8 bits)
endmodule

module MAR (
  input  Clock,
  input  WE,
  input  [3:0] Din,
  input  OE,
  output [3:0] Dout,
  output [3:0] Stored_Data
);

  Memory_Cell o (
    .Clock(Clock), .WE(WE), .Din(Din[0]), .OE(OE), .Dout(Dout[0]), .Stored_Data(Stored_Data[0]));  // open: Reset
  Memory_Cell _1 (
    .Clock(Clock), .WE(WE), .Din(Din[1]), .OE(OE), .Dout(Dout[1]), .Stored_Data(Stored_Data[1]));  // open: Reset
  Memory_Cell _2 (
    .Clock(Clock), .WE(WE), .Din(Din[2]), .OE(OE), .Dout(Dout[2]), .Stored_Data(Stored_Data[2]));  // open: Reset
  Memory_Cell _3 (
    .Clock(Clock), .WE(WE), .Din(Din[3]), .OE(OE), .Dout(Dout[3]), .Stored_Data(Stored_Data[3]));  // open: Reset

  // Notes on the sheet:
  //   MAR
endmodule

module ALU (
  input  [7:0] Reg_A,
  input  [7:0] Reg_B,
  input  OE,
  output [7:0] Dout,
  output [7:0] ALU_Result,
  output Carry_Out
);

  Adder adder_1 (.a(Reg_A), .b(Reg_B), .out(ALU_Result), .cout(Carry_Out));  // open: cin
  assign Dout = OE ? ALU_Result : 8'bz;  // Controlled_Buffer controlled_buffer_1

  // Notes on the sheet:
  //   ALU
endmodule
